# Fritzing sketch Fussen (saved by Fritzing 0.9.4)
breadboards: 3

parts:
  CPU1 = Arduino Mega 2560 (Rev3)
  U1 = 74HC595 [package="DIP16 [THT]"]
  U2 = 74HC595 [package="DIP16 [THT]"]
  U3 = 74HC595 [package="DIP16 [THT]"]
  U4 = 74HC595 [package="DIP16 [THT]"]
  R1 = Resistor [tolerance=±1% resistance=22k package=THT]  # not connected
  R2 = Resistor [tolerance=±1% resistance=33k package=THT]  # not connected
  R3 = Resistor [tolerance=±1% resistance=22k package=THT]
  R4 = Resistor [tolerance=±1% resistance=33k package=THT]
  R5 = Resistor [tolerance=±1% resistance=22k package=THT]
  R6 = Resistor [tolerance=±1% resistance=33k package=THT]
  R7 = Resistor [tolerance=±1% resistance=22k package=THT]
  R8 = Resistor [tolerance=±1% resistance=33k package=THT]
  R9 = Resistor [tolerance=±1% resistance=22k package=THT]
  R10 = Resistor [tolerance=±1% resistance=33k package=THT]
  R11 = Resistor [tolerance=±1% resistance=22k package=THT]
  R12 = Resistor [tolerance=±1% resistance=22k package=THT]
  R15 = Resistor [tolerance=±1% resistance=33k package=THT]  # not connected
  R16 = Resistor [tolerance=±0.5% resistance=15k power=25mW package=THT]
  R17 = Resistor [tolerance=±1% resistance=33k package=THT]
  R18 = Resistor [tolerance=±1% resistance=22k package=THT]
  R19 = Resistor [tolerance=±1% resistance=33k package=THT]
  R20 = Resistor [tolerance=±0.5% resistance=33k power=25mW package=THT]
  R21 = Resistor [tolerance=±0.5% resistance=22k power=25mW package=THT]  # not connected
  R22 = Resistor [tolerance=±1% resistance=22k package=THT]  # not connected
  R23 = Resistor [tolerance=±1% resistance=22k package=THT]  # not connected
  R24 = Resistor [tolerance=±1% resistance=22k package=THT]  # not connected
  Shield1 = Arduino Motor Shield (Rev3)
  C1 = Electrolytic Capacitor [capacitance=10µF voltage=35V package="100 mil [THT, electrolytic]"]
  R33 = Resistor [tolerance=±5% resistance=1k package=THT]
  SP1 = SPEAKER [package=pcb_mount_speaker]
  L1 = Solenoid [part_number="Turnout 1 Straight"]
  L2 = Solenoid [part_number="Turnout 1 Throw"]
  L3 = Solenoid [part_number="Turnout 2 Straight"]
  LED1 = DUO LED RG [part_number="Turnout 1 Signal" package="5 mm [THT]"]
  LED2 = DUO LED RG [part_number="Turnout 2 Signal" package="5 mm [THT]"]
  L4 = Solenoid [part_number="Turnout 2 Throw"]
  M1 = DSN-MINI-360
  Adapter1 = Open-Smart ESP-01 Adapter [package=Board]
  DFRobot_DFPlayer_Mini1 = DFRobot DFPlayer Mini [part_number=DFR0299]
  M2 = MOSFET4 UO4 [part_number=MOSFET4 package=THT]
  VCC1 = TalentCell Power Bank [part_number=YB12011000-USB]

nets (from the schematic view):
  N1: CPU1.A13, U4.DS
  N2: CPU1.A14, U1.ST_CP, U2.ST_CP, U3.ST_CP, U4.ST_CP, C1.+
  N3: CPU1.A15, U1.SH_CP, U2.SH_CP, U3.SH_CP, U4.SH_CP
  N4: CPU1.A0, Shield1.A0
  N5: CPU1.A1, Shield1.A1
  N6: CPU1.D19/RX1, DFRobot_DFPlayer_Mini1.TX
  N7: CPU1.D18/TX1, R33.Pin_0
  N8: CPU1.D15/RX3, Adapter1.pin4
  N9: CPU1.D14/TX3, Adapter1.pin3
  GND: CPU1.GND, U1.GND, U1.OE, U2.GND, U2.OE, U3.GND, U3.OE, U4.GND, U4.OE, Shield1.GND, C1.-, M1.Pin_2, M1.Pin_4, Adapter1.pin2, M2.GND, VCC1.pin_4, VCC1.pin_5, VCC1.pin_6
  N10: CPU1.D12_PWM, Shield1.D12/DirA
  N11: CPU1.D11_PWM, Shield1.D11_PWM/B
  N12: CPU1.IOREF, Shield1.5V
  N13: CPU1.D2_PWM, Shield1.D13/DirB, Shield1.D2
  N14: CPU1.D3_PWM, Shield1.D3_PWM/A
  N15: CPU1.D22, M2.SIG1
  N16: CPU1.D23, M2.SIG2
  N17: CPU1.D24, M2.SIG3
  N18: CPU1.D25, M2.SIG4
  VCC: U1.MR, U1.VCC, U2.MR, U2.VCC, U3.MR, U3.VCC, U4.MR, U4.VCC, M1.Pin_1, Adapter1.pin1, VCC1.pin_1
  N19: U1.DS, U2.Q7'
  N20: U2.DS, U3.Q7'
  N21: U2.Q0, R3.Pin_0
  N22: U3.Q1, R19.Pin_0
  N23: U3.Q2, R18.Pin_0
  N24: U3.Q3, R17.Pin_0
  N25: U3.Q4, R16.Pin_0
  N26: U3.Q5, R20.Pin_0
  N27: U3.DS, U4.Q7'
  N28: U3.Q0, R12.Pin_0
  N29: U4.Q1, R10.Pin_0
  N30: U4.Q2, R9.Pin_0
  N31: U4.Q3, R8.Pin_0
  N32: U4.Q4, R7.Pin_1
  N33: U4.Q5, R6.Pin_0
  N34: U4.Q6, R5.Pin_0
  N35: U4.Q7, R4.Pin_0
  N36: U4.Q0, R11.Pin_0
  N37: R8.Pin_1, LED2.red_anode
  N38: R10.Pin_1, LED1.red_anode
  N39: R11.Pin_1, LED1.green_anode
  N40: Shield1.VMOT, VCC1.pin_2
  N41: R33.Pin_1, DFRobot_DFPlayer_Mini1.RX
  N42: SP1.+, DFRobot_DFPlayer_Mini1.SPK_1
  N43: SP1.-, DFRobot_DFPlayer_Mini1.SPK_2
  N44: L1.pin1, M2.V1-
  N45: L1.pin2, M2.V1+
  N46: L2.pin1, M2.V2-
  N47: L2.pin2, M2.V2+
  N48: L3.pin1, M2.V3-
  N49: L3.pin2, M2.V3+
  N50: L4.pin1, M2.V4-
  N51: L4.pin2, M2.V4+
  N52: M1.Pin_3, DFRobot_DFPlayer_Mini1.VCC
  N53: DFRobot_DFPlayer_Mini1.GND-1, DFRobot_DFPlayer_Mini1.GND-2
  N54: M2.VIN, VCC1.pin_3

notes:
  -
  +

custom parts:
  DSN-MINI-360: Step-down DC-DC Converter MPS MP2307DN buck regulator IC 4.75 – 23VDC input voltage 1.0 – 17VDC selectable output voltage 3A surge current, 1.8A continuous rated current Maximum conversion efficiency of 95% (5Vin, 3.3Vout ~200mA output) 340kHz switching frequency 30mV no-load output ripple 0.5% load regulation 2.5% voltage regulation -40 to +85°C operational temperature range Built-in 160°C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
  Open-Smart ESP-01 Adapter: Serial adapter for ESP-01 wifi board.
  MOSFET4 UO4: Breakout board for four (4) IFR540N MOSFET transistor channels. The module is designed to switch heavy DC loads from four digital pins of a microcontroller. Its main purpose is to provide a low cost way to drive DC motor, solenoids or LED arrays, but the module can be used to control most high current DC loads. Screw terminals are provided to interface to the loads and external power source.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
  TalentCell Power Bank: Mulitple output rechargeable power cell 12v - connector, postive center pin 9v - connector, positive center pin 5v - USB connector 11,000mAh
